// Digital circuit part_b.dig as structural Verilog
module part_b (
  input  in_0,
  input  in_1,
  input  in_2,
  output out_0
);

  wire and_1_out, and_2_out, and_3_out, and_4_out, and_5_out, not_1_out, not_2_out, not_3_out, not_4_out,
       not_5_out, not_6_out, not_7_out, not_8_out;

  and and_1 (and_1_out, not_1_out, not_2_out, not_3_out);
  not not_1 (not_1_out, in_0);
  not not_2 (not_2_out, in_1);
  not not_3 (not_3_out, in_2);
  and and_2 (and_2_out, not_4_out, in_1, not_5_out);
  not not_4 (not_4_out, in_0);
  not not_5 (not_5_out, in_2);
  and and_3 (and_3_out, in_0, not_6_out, not_7_out);
  not not_6 (not_6_out, in_1);
  not not_7 (not_7_out, in_2);
  and and_4 (and_4_out, in_0, in_1, not_8_out);
  not not_8 (not_8_out, in_2);
  and and_5 (and_5_out, in_0, in_1, in_2);
  or or_1 (out_0, and_1_out, and_2_out, and_3_out, and_4_out, and_5_out);
endmodule

/* Test case part b test:
in_0 in_1 in_2 out_0 

 0 0 0 1
 0 0 1 0
 0 1 0 1
 0 1 1 0
 1 0 0 1
 1 0 1 0
 1 1 0 1
 1 1 1 1
*/
