// Digital circuit part_c.dig as structural Verilog
module part_c (
  input  in_0,
  input  in_1,
  input  in_2,
  output out_0
);

  wire nfet_1_s, nfet_5_s, nfet_9_s, nfet_11_s, pfet_1_d, pfet_3_d, pfet_4_d, pfet_5_d, pfet_6_d, pfet_8_d,
       pfet_9_d, pfet_11_d, pfet_12_d, pfet_14_d, pfet_15_d, pfet_16_d;

  PFET pfet_1 (.G(in_0), .S(1'b0), .D(pfet_1_d));
  PFET pfet_2 (.G(in_2), .S(1'b0), .D(pfet_1_d));
  NFET nfet_1 (.G(in_2), .D(pfet_1_d), .S(nfet_1_s));
  NFET nfet_2 (.G(in_0), .D(nfet_1_s), .S(1'b1));
  PFET pfet_3 (.G(in_0), .S(1'b1), .D(pfet_3_d));
  NFET nfet_3 (.G(in_0), .D(pfet_3_d), .S(1'b0));
  PFET pfet_4 (.G(in_0), .S(1'b0), .D(pfet_4_d));
  PFET pfet_5 (.G(pfet_1_d), .S(1'b0), .D(pfet_5_d));
  NFET nfet_4 (.G(pfet_1_d), .D(pfet_5_d), .S(1'b1));
  NFET nfet_5 (.G(in_1), .D(pfet_4_d), .S(nfet_5_s));
  NFET nfet_6 (.G(in_0), .D(nfet_5_s), .S(1'b1));
  PFET pfet_6 (.G(in_1), .S(1'b1), .D(pfet_6_d));
  NFET nfet_7 (.G(in_1), .D(pfet_6_d), .S(1'b0));
  PFET pfet_7 (.G(in_1), .S(1'b0), .D(pfet_4_d));
  PFET pfet_8 (.G(pfet_4_d), .S(1'b0), .D(pfet_8_d));
  NFET nfet_8 (.G(pfet_4_d), .D(pfet_8_d), .S(1'b1));
  PFET pfet_9 (.G(pfet_3_d), .S(1'b0), .D(pfet_9_d));
  PFET pfet_10 (.G(pfet_6_d), .S(1'b0), .D(pfet_9_d));
  NFET nfet_9 (.G(pfet_6_d), .D(pfet_9_d), .S(nfet_9_s));
  NFET nfet_10 (.G(pfet_3_d), .D(nfet_9_s), .S(1'b1));
  PFET pfet_11 (.G(pfet_8_d), .S(1'b0), .D(pfet_11_d));
  NFET nfet_11 (.G(pfet_5_d), .D(pfet_11_d), .S(nfet_11_s));
  NFET nfet_12 (.G(pfet_8_d), .D(nfet_11_s), .S(1'b1));
  PFET pfet_12 (.G(pfet_9_d), .S(1'b0), .D(pfet_12_d));
  NFET nfet_13 (.G(pfet_9_d), .D(pfet_12_d), .S(1'b1));
  PFET pfet_13 (.G(pfet_5_d), .S(1'b0), .D(pfet_11_d));
  PFET pfet_14 (.G(pfet_11_d), .S(1'b0), .D(pfet_14_d));
  NFET nfet_14 (.G(pfet_11_d), .D(pfet_14_d), .S(1'b1));
  PFET pfet_15 (.G(pfet_12_d), .S(1'b0), .D(pfet_15_d));
  PFET pfet_16 (.G(pfet_14_d), .S(pfet_15_d), .D(pfet_16_d));
  NFET nfet_15 (.G(pfet_12_d), .D(pfet_16_d), .S(1'b1));
  NFET nfet_16 (.G(pfet_14_d), .D(pfet_16_d), .S(1'b1));
  PFET pfet_17 (.G(pfet_16_d), .S(1'b0), .D(out_0));
  NFET nfet_17 (.G(pfet_16_d), .D(out_0), .S(1'b1));
endmodule

/* Test case part c test:
in_0 in_1 in_2  out_0
0 0 0  1
0 0 1  1
0 1 0  0
0 1 1  0
1 0 0  0
1 0 1  0
1 1 0  0
1 1 1  1
*/
