// Digital circuit lab2_part2.dig as structural Verilog
module lab2_part2 (
  input  in0,
  input  in1,
  input  in2,
  input  in3,
  output seg_a,
  output seg_f,
  output seg_b,
  output seg_g,
  output seg_e,
  output seg_c,
  output seg_d,
  output seg_dp,
  output sign_a,
  output sign_f,
  output sign_b,
  output sign_g,
  output sign_e,
  output sign_c,
  output sign_d,
  output sign_dp
);

  wire [7:0] con, con1;

  Seven_Seg seven_seg_1 (
    .a(sign_a), .b(sign_b), .c(sign_c), .d(sign_d), .e(sign_e), .f(sign_f), .g(sign_g), .dp(sign_dp));
  Seven_Seg seven_seg_2 (.a(seg_a), .b(seg_b), .c(seg_c), .d(seg_d), .e(seg_e), .f(seg_f), .g(seg_g), .dp(seg_dp));
  Multiplexer #(.Selector_Bits(3), .Bits(8)) multiplexer_1 (
    .sel({in2, in1, in0}), .in_0(8'h3f), .in_1(8'h6), .in_2(8'h5b), .in_3(8'h4f), .in_4(8'h66), .in_5(8'h6d),
    .in_6(8'h7d), .in_7(8'h7), .out(con));
  Multiplexer #(.Selector_Bits(3), .Bits(8)) multiplexer_2 (
    .sel({in2, in1, in0}), .in_0(8'h7f), .in_1(8'h7), .in_2(8'h7d), .in_3(8'h6d), .in_4(8'h66), .in_5(8'h4f),
    .in_6(8'h5b), .in_7(8'h6), .out(con1));
  Multiplexer #(.Bits(8)) multiplexer_3 (
    .sel(in3), .in_0({8{1'b0}}), .in_1(8'h40),
    .out({sign_dp, sign_g, sign_f, sign_e, sign_d, sign_c, sign_b, sign_a}));
  Multiplexer #(.Bits(8)) multiplexer_4 (
    .sel(in3), .in_0(con), .in_1(con1), .out({seg_dp, seg_g, seg_f, seg_e, seg_d, seg_c, seg_b, seg_a}));

  // Notes on the sheet:
  //   Interface (do not edit the content inside this box)
  //   Outputs:
  //   Inputs
  //   Sign
  //   Decimal Number
endmodule

/* Test case:
in3 in2 in1 in0  sign_a sign_b sign_c sign_d sign_e sign_f sign_g  seg_a seg_b seg_c seg_d seg_e seg_f seg_g
 0   0   0   0    0      0      0      0      0      0      0       1     1     1     1     1     1     0
*/
